// Logisim project mips_single_cycle.circ as structural Verilog: 7 circuits, main circuit reg_file
module main (
);

  wire alu_1_zero, ALUSrc, and_1_out, Branch, clock_1_out, clock_2_out, clock_3_out, Jump, MemRead, MemToReg,
       MemWrite, RegDst, RegWrite;
  wire [1:0] ALUOp;
  wire [3:0] alu_ctrl_1_alucontrol;
  wire [4:0] multiplexer_1_out;
  wire [5:0] opcode;
  wire [27:2] instr_mem_1_instr;
  wire [31:0] adder_1_out, adder_2_out, alu_1_r, bit_extender_1_out, data_mem_1_read_data, multiplexer_2_out,
       multiplexer_3_out, multiplexer_4_out, PC_q, reg_file_1_rd1, reg_file_1_rd2, shifter_1_out, Write_Data;

  Clock clock_1 (.out(clock_1_out));
  Register #(.width(32)) PC (.D(multiplexer_4_out), .clk(clock_1_out), .Q(PC_q));  // open: en, clr
  Adder #(.width(32)) adder_1 (.a(32'h4), .b(PC_q), .out(adder_1_out));  // open: cin, cout
  instr_mem instr_mem_1 (.addr(PC_q[23:0]), .instr({opcode, instr_mem_1_instr}));
  control control_1 (
    .opcode(opcode), .RegDst(RegDst), .ALUSrc(ALUSrc), .MemToReg(MemToReg), .RegWrite(RegWrite),
    .MemRead(MemRead), .MemWrite(MemWrite), .Branch(Branch), .Jump(Jump), .ALUOp1(ALUOp[1]), .ALUOp0(ALUOp[0]));
  Multiplexer #(.width(5)) multiplexer_1 (
    .in0(instr_mem_1_instr[22:18]), .in1(instr_mem_1_instr[17:13]), .out(multiplexer_1_out), .sel(RegDst));
  assign bit_extender_1_out = {{16{instr_mem_1_instr[17]}}, instr_mem_1_instr[17:2]};  // Bit_Extender bit_extender_1
  Clock clock_2 (.out(clock_2_out));
  reg_file reg_file_1 (
    .Write_Register(multiplexer_1_out), .RR2(instr_mem_1_instr[22:18]), .RR1(instr_mem_1_instr[27:23]),
    .CLK(clock_2_out), .RegWrite(RegWrite), .Write_Data(Write_Data), .RD2(reg_file_1_rd2),
    .RD1(reg_file_1_rd1));
  Multiplexer #(.width(32)) multiplexer_2 (
    .in0(reg_file_1_rd2), .in1(bit_extender_1_out), .out(multiplexer_2_out), .sel(ALUSrc));
  Shifter #(.width(32)) shifter_1 (.in(bit_extender_1_out), .\dist (5'b00010), .out(shifter_1_out));
  Adder #(.width(32)) adder_2 (.a(adder_1_out), .b(shifter_1_out), .out(adder_2_out));  // open: cin, cout
  and and_1 (and_1_out, Branch, alu_1_zero);
  ALU alu_1 (
    .B(multiplexer_2_out), .A(reg_file_1_rd1), .ALUControl(alu_ctrl_1_alucontrol), .R(alu_1_r),
    .Zero(alu_1_zero));
  alu_ctrl alu_ctrl_1 (.alu_op(ALUOp), .funct(instr_mem_1_instr[7:2]), .ALUControl(alu_ctrl_1_alucontrol));
  Multiplexer #(.width(32)) multiplexer_3 (
    .in0(adder_1_out), .in1(adder_2_out), .out(multiplexer_3_out), .sel(and_1_out));
  Clock clock_3 (.out(clock_3_out));
  data_mem data_mem_1 (
    .MemRead(MemRead), .Address(alu_1_r), .MemWrite(MemWrite), .Write_Data(reg_file_1_rd2),
    .CLK(clock_3_out), .Read_Data(data_mem_1_read_data));
  Multiplexer #(.width(32)) multiplexer_4 (
    .in0(multiplexer_3_out), .in1({multiplexer_3_out[31:28], instr_mem_1_instr, 2'b00}),
    .out(multiplexer_4_out), .sel(Jump));
  Multiplexer #(.width(32)) multiplexer_5 (.in0(alu_1_r), .in1(data_mem_1_read_data), .out(Write_Data), .sel(MemToReg));

  // Notes on the sheet:
  //   PC + 4
  //   opcode
  //   rs
  //   rt
  //   funct
  //   imm
  //   j addr
  //   rd
  //   shamt
  //   Camino de Datos de MIPS 32 bits. Un ciclo una instruccion
  //   function code
  //   j addr (26 bits)
  //   PC + 4
endmodule

module reg_file (
  input  [4:0] RR1,
  input  CLK,
  input  RegWrite,
  input  [4:0] Write_Register,
  input  [31:0] Write_Data,
  input  [4:0] RR2,
  output [31:0] RD1,
  output [31:0] RD2
);

  wire CLK_t, decoder_1_out0, decoder_1_out1, decoder_1_out2, decoder_1_out3, decoder_1_out4, decoder_1_out5,
       decoder_1_out6, decoder_1_out7, decoder_1_out8, decoder_1_out9, decoder_1_out10, decoder_1_out11,
       decoder_1_out12, decoder_1_out13, decoder_1_out14, decoder_1_out15, decoder_1_out16, decoder_1_out17,
       decoder_1_out18, decoder_1_out19, decoder_1_out20, decoder_1_out21, decoder_1_out22, decoder_1_out23,
       decoder_1_out24, decoder_1_out25, decoder_1_out26, decoder_1_out27, decoder_1_out28, decoder_1_out29,
       decoder_1_out30, decoder_1_out31;
  wire [31:0] a0_q, a1_q, a2_q, a3_q, at_q, fp_q, gp_q, k0_q, k1_q, ra_q, s0_q, s1_q, s2_q, s3_q, s4_q, s5_q,
       s6_q, s7_q, sp_q, t0_q, t1_q, t2_q, t3_q, t4_q, t5_q, t6_q, t7_q, t8_q, t9_q, v0_q, v1_q, zero_q;

  Decoder #(.enable("false"), .select(5)) decoder_1 (
    .out0(decoder_1_out0), .out1(decoder_1_out1), .out2(decoder_1_out2), .out3(decoder_1_out3),
    .out4(decoder_1_out4), .out5(decoder_1_out5), .out6(decoder_1_out6), .out7(decoder_1_out7),
    .out8(decoder_1_out8), .out9(decoder_1_out9), .out10(decoder_1_out10), .out11(decoder_1_out11),
    .out12(decoder_1_out12), .out13(decoder_1_out13), .out14(decoder_1_out14), .out15(decoder_1_out15),
    .out16(decoder_1_out16), .out17(decoder_1_out17), .out18(decoder_1_out18), .out19(decoder_1_out19),
    .out20(decoder_1_out20), .out21(decoder_1_out21), .out22(decoder_1_out22), .out23(decoder_1_out23),
    .out24(decoder_1_out24), .out25(decoder_1_out25), .out26(decoder_1_out26), .out27(decoder_1_out27),
    .out28(decoder_1_out28), .out29(decoder_1_out29), .out30(decoder_1_out30), .out31(decoder_1_out31),
    .sel(Write_Register));
  and and_1 (CLK_t, CLK, RegWrite);
  Register #(.width(32)) zero (.D(Write_Data), .en(decoder_1_out0), .clk(CLK_t), .Q(zero_q));  // open: clr
  Register #(.width(32)) a0 (.D(Write_Data), .en(decoder_1_out4), .clk(CLK_t), .Q(a0_q));  // open: clr
  Register #(.width(32)) t0 (.D(Write_Data), .en(decoder_1_out8), .clk(CLK_t), .Q(t0_q));  // open: clr
  Register #(.width(32)) t4 (.D(Write_Data), .en(decoder_1_out12), .clk(CLK_t), .Q(t4_q));  // open: clr
  Register #(.width(32)) s0 (.D(Write_Data), .en(decoder_1_out16), .clk(CLK_t), .Q(s0_q));  // open: clr
  Register #(.width(32)) s4 (.D(Write_Data), .en(decoder_1_out20), .clk(CLK_t), .Q(s4_q));  // open: clr
  Register #(.width(32)) t8 (.D(Write_Data), .en(decoder_1_out24), .clk(CLK_t), .Q(t8_q));  // open: clr
  Register #(.width(32)) gp (.D(Write_Data), .en(decoder_1_out28), .clk(CLK_t), .Q(gp_q));  // open: clr
  Register #(.width(32)) at (.D(Write_Data), .en(decoder_1_out1), .clk(CLK_t), .Q(at_q));  // open: clr
  Register #(.width(32)) a1 (.D(Write_Data), .en(decoder_1_out5), .clk(CLK_t), .Q(a1_q));  // open: clr
  Register #(.width(32)) t1 (.D(Write_Data), .en(decoder_1_out9), .clk(CLK_t), .Q(t1_q));  // open: clr
  Register #(.width(32)) t5 (.D(Write_Data), .en(decoder_1_out13), .clk(CLK_t), .Q(t5_q));  // open: clr
  Register #(.width(32)) s1 (.D(Write_Data), .en(decoder_1_out17), .clk(CLK_t), .Q(s1_q));  // open: clr
  Register #(.width(32)) s5 (.D(Write_Data), .en(decoder_1_out21), .clk(CLK_t), .Q(s5_q));  // open: clr
  Register #(.width(32)) t9 (.D(Write_Data), .en(decoder_1_out25), .clk(CLK_t), .Q(t9_q));  // open: clr
  Register #(.width(32)) sp (.D(Write_Data), .en(decoder_1_out29), .clk(CLK_t), .Q(sp_q));  // open: clr
  Register #(.width(32)) v0 (.D(Write_Data), .en(decoder_1_out2), .clk(CLK_t), .Q(v0_q));  // open: clr
  Register #(.width(32)) a2 (.D(Write_Data), .en(decoder_1_out6), .clk(CLK_t), .Q(a2_q));  // open: clr
  Register #(.width(32)) t2 (.D(Write_Data), .en(decoder_1_out10), .clk(CLK_t), .Q(t2_q));  // open: clr
  Register #(.width(32)) t6 (.D(Write_Data), .en(decoder_1_out14), .clk(CLK_t), .Q(t6_q));  // open: clr
  Register #(.width(32)) s2 (.D(Write_Data), .en(decoder_1_out18), .clk(CLK_t), .Q(s2_q));  // open: clr
  Register #(.width(32)) s6 (.D(Write_Data), .en(decoder_1_out22), .clk(CLK_t), .Q(s6_q));  // open: clr
  Register #(.width(32)) k0 (.D(Write_Data), .en(decoder_1_out26), .clk(CLK_t), .Q(k0_q));  // open: clr
  Register #(.width(32)) fp (.D(Write_Data), .en(decoder_1_out30), .clk(CLK_t), .Q(fp_q));  // open: clr
  Register #(.width(32)) v1 (.D(Write_Data), .en(decoder_1_out3), .clk(CLK_t), .Q(v1_q));  // open: clr
  Register #(.width(32)) a3 (.D(Write_Data), .en(decoder_1_out7), .clk(CLK_t), .Q(a3_q));  // open: clr
  Register #(.width(32)) t3 (.D(Write_Data), .en(decoder_1_out11), .clk(CLK_t), .Q(t3_q));  // open: clr
  Register #(.width(32)) t7 (.D(Write_Data), .en(decoder_1_out15), .clk(CLK_t), .Q(t7_q));  // open: clr
  Register #(.width(32)) s3 (.D(Write_Data), .en(decoder_1_out19), .clk(CLK_t), .Q(s3_q));  // open: clr
  Register #(.width(32)) s7 (.D(Write_Data), .en(decoder_1_out23), .clk(CLK_t), .Q(s7_q));  // open: clr
  Register #(.width(32)) k1 (.D(Write_Data), .en(decoder_1_out27), .clk(CLK_t), .Q(k1_q));  // open: clr
  Register #(.width(32)) ra (.D(Write_Data), .en(decoder_1_out31), .clk(CLK_t), .Q(ra_q));  // open: clr
  Multiplexer #(.select(5), .width(32)) multiplexer_1 (
    .in0(zero_q), .in1(at_q), .in2(v0_q), .in3(v1_q), .in4(a0_q), .in5(a1_q), .in6(a2_q), .in7(a3_q),
    .in8(t0_q), .in9(t1_q), .in10(t2_q), .in11(t3_q), .in12(t4_q), .in13(t5_q), .in14(t6_q), .in15(t7_q),
    .in16(s0_q), .in17(s1_q), .in18(s2_q), .in19(s3_q), .in20(s4_q), .in21(s5_q), .in22(s6_q), .in23(s7_q),
    .in24(t8_q), .in25(t9_q), .in26(k0_q), .in27(k1_q), .in28(gp_q), .in29(sp_q), .in30(fp_q), .in31(ra_q),
    .out(RD1), .sel(RR1));
  Multiplexer #(.select(5), .width(32)) multiplexer_2 (
    .in0(zero_q), .in1(at_q), .in2(v0_q), .in3(v1_q), .in4(a0_q), .in5(a1_q), .in6(a2_q), .in7(a3_q),
    .in8(t0_q), .in9(t1_q), .in10(t2_q), .in11(t3_q), .in12(t4_q), .in13(t5_q), .in14(t6_q), .in15(t7_q),
    .in16(s0_q), .in17(s1_q), .in18(s2_q), .in19(s3_q), .in20(s4_q), .in21(s5_q), .in22(s6_q), .in23(s7_q),
    .in24(t8_q), .in25(t9_q), .in26(k0_q), .in27(k1_q), .in28(gp_q), .in29(sp_q), .in30(fp_q), .in31(ra_q),
    .out(RD2), .sel(RR2));
endmodule

module instr_mem (
  input  [23:0] addr,
  output [31:0] instr
);

  ROM #(.addrWidth(24), .dataWidth(32)) rom_1 (.addr(addr), .data(instr));

  // Notes on the sheet:
  //   contents of rom_1 (hex, n*v repeats v):
  //   12a4020
endmodule

module ALU (
  input  [31:0] A,
  input  [31:0] B,
  input  [3:0] ALUControl,
  output Zero,
  output [31:0] R
);

  wire [31:0] adder_1_out, and_1_out, multiplexer_1_out, multiplexer_2_out, not_1_out, not_2_out, or_1_out;

  assign not_1_out = ~A;  // NOT_Gate not_1, 32 bits wide
  assign not_2_out = ~B;  // NOT_Gate not_2, 32 bits wide
  Multiplexer #(.width(32)) multiplexer_1 (.in0(A), .in1(not_1_out), .out(multiplexer_1_out), .sel(ALUControl[3]));
  Multiplexer #(.width(32)) multiplexer_2 (.in0(B), .in1(not_2_out), .out(multiplexer_2_out), .sel(ALUControl[2]));
  assign and_1_out = multiplexer_1_out & multiplexer_2_out;  // AND_Gate and_1, 32 bits wide
  assign or_1_out = multiplexer_1_out | multiplexer_2_out;  // OR_Gate or_1, 32 bits wide
  Adder #(.width(32)) adder_1 (
    .a(multiplexer_1_out), .b(multiplexer_2_out), .out(adder_1_out), .cin(ALUControl[2]));  // open: cout
  Multiplexer #(.select(2), .width(32)) multiplexer_3 (
    .in0(and_1_out), .in1(or_1_out), .in2(adder_1_out), .out(R), .sel(ALUControl[1:0]));  // open: in3
  Comparator #(.width(32)) comparator_1 (.a({32{1'b0}}), .b(R), .eq(Zero));  // open: gt, lt

  // Notes on the sheet:
  //   A Inv
  //   B Inv
  //   MUX
endmodule

module data_mem (
  input  MemRead,
  input  [31:0] Address,
  input  MemWrite,
  input  [31:0] Write_Data,
  input  CLK,
  output [31:0] Read_Data
);

  RAM #(.addrWidth(24), .dataWidth(32)) ram_1 (
    .addr(Address[25:2]), .we(MemWrite), .oe(MemRead), .clk(CLK), .din(Write_Data), .dout(Read_Data));
endmodule

module control (
  input  [5:0] opcode,
  output RegDst,
  output ALUSrc,
  output MemToReg,
  output RegWrite,
  output MemRead,
  output MemWrite,
  output Branch,
  output Jump,
  output ALUOp1,
  output ALUOp0
);

  wire and_6_out, and_7_out;

  and and_1 (ALUOp0, ~opcode[5], ~opcode[4], ~opcode[3], opcode[2], ~opcode[1], ~opcode[0]);  // AND_Gate
  and and_2 (ALUOp1, ~opcode[5], ~opcode[4], ~opcode[3], ~opcode[2], ~opcode[1], ~opcode[0]);  // AND_Gate
  and and_3 (MemRead, opcode[5], ~opcode[4], ~opcode[3], ~opcode[2], opcode[1], opcode[0]);  // AND_Gate
  and and_4 (MemWrite, opcode[5], ~opcode[4], opcode[3], ~opcode[2], opcode[1], opcode[0]);  // AND_Gate
  and and_5 (Jump, ~opcode[5], ~opcode[4], ~opcode[3], ~opcode[2], opcode[1], ~opcode[0]);  // AND_Gate
  and and_6 (and_6_out, ~opcode[5], ~opcode[4], opcode[3], ~opcode[2], ~opcode[1], ~opcode[0]);  // AND_Gate
  and and_7 (and_7_out, ~opcode[5], ~opcode[4], opcode[3], opcode[2], ~opcode[1], opcode[0]);  // AND_Gate
  or or_1 (ALUSrc, and_7_out, and_6_out, MemWrite, MemRead);
  or or_2 (RegWrite, and_7_out, and_6_out, MemRead, ALUOp1);

  assign Branch = ALUOp0;
  assign MemToReg = MemRead;
  assign RegDst = ALUOp1;

  // Notes on the sheet:
  //   beq
  //   Tipo R
  //   lw
  //   sw
  //   j
  //   addi
  //   ori
endmodule

module alu_ctrl (
  input  [1:0] alu_op,
  input  [5:0] funct,
  output [3:0] ALUControl
);

  wire and_1_out;

  and and_1 (and_1_out, funct[1], alu_op[1]);
  or or_1 (ALUControl[1], ~funct[2], ~alu_op[1]);  // OR_Gate
  and and_2 (ALUControl[0], funct[2], funct[0], alu_op[1]);
  or or_2 (ALUControl[2], alu_op[0], and_1_out);

  assign ALUControl[3] = 1'b0;
endmodule
